// Logisim project 8_bit_cpu_test.circ as structural Verilog: 10 circuits, main circuit main
module main (
  input  in_1
);

  wire button_1_out, clock_1_out, clock_2_out, cpu_1_ram_out, cpu_1_ram_write;
  wire [3:0] cpu_1_ram_addr;
  wire [7:0] cpu_1_display, cpu_1_ram_data_in, cpu_1_rom_addr, ram_1_dout, rom_1_data, undriven;

  ROM rom_1 (.addr(cpu_1_rom_addr), .data(rom_1_data));
  Clock clock_1 (.out(clock_1_out));
  Button button_1 (.out(button_1_out));
  RAM #(.addrWidth(4)) ram_1 (
    .addr(cpu_1_ram_addr), .we(cpu_1_ram_write), .oe(cpu_1_ram_out), .clk(clock_1_out),
    .din(cpu_1_ram_data_in), .dout(ram_1_dout));
  // DipSwitch dipswitch_1: pin names not known
  Clock clock_2 (.out(clock_2_out));
  CPU cpu_1 (
    .Rom_In(rom_1_data), .Input_In(undriven), .Input_Done(button_1_out), .Reset(in_1),
    .Ram_Data_Out(ram_1_dout), .Clock(clock_2_out), .Display(cpu_1_display), .Rom_Addr(cpu_1_rom_addr),
    .Ram_Addr(cpu_1_ram_addr), .Ram_Write(cpu_1_ram_write), .Ram_Out(cpu_1_ram_out),
    .Ram_Data_In(cpu_1_ram_data_in));
  _7_Segment_Display u_7_segment_display_1 ();  // open: g, f, a, b, e, d, c, dp
  // BCD_to_7_Segment_decoder bcd_to_7_segment_decoder_1: pin names not known
  _7_Segment_Display u_7_segment_display_2 ();  // open: g, f, a, b, e, d, c, dp
  // BCD_to_7_Segment_decoder bcd_to_7_segment_decoder_2: pin names not known
  // Binary_to_BCD_converter #(.binvalue(8)) binary_to_bcd_converter_1: pin names not known; wires that end beside it: cpu_1_display
  _7_Segment_Display u_7_segment_display_3 ();  // open: g, f, a, b, e, d, c, dp
  // BCD_to_7_Segment_decoder bcd_to_7_segment_decoder_3: pin names not known

  // Notes on the sheet:
  //   contents of rom_1 (hex, n*v repeats v):
  //   21 30 c0 40 10 a3 250*c0
endmodule

module Alu (
  input  [7:0] A_In,
  input  [7:0] B_In,
  input  ADD,
  input  SUB,
  input  A_B_AND,
  input  A_B_OR,
  input  A_B_XOR,
  input  A_NOT,
  output [7:0] Alu_OUT
);

  wire [7:0] adder_1_out, and_1_out, not_1_out, or_1_out, subtractor_1_out, xor_1_out;

  Adder adder_1 (.a(A_In), .b(B_In), .out(adder_1_out));  // open: cin, cout
  Subtractor subtractor_1 (.a(A_In), .b(B_In), .out(subtractor_1_out));  // open: bin, bout
  assign and_1_out = A_In & B_In;  // AND_Gate and_1, 8 bits wide
  assign or_1_out = A_In | B_In;  // OR_Gate or_1, 8 bits wide
  assign xor_1_out = A_In ^ B_In;  // XOR_Gate xor_1, 8 bits wide
  assign not_1_out = ~A_In;  // NOT_Gate not_1, 8 bits wide
  assign Alu_OUT = ADD ? adder_1_out : 8'bz;  // Controlled_Buffer controlled_buffer_1
  assign Alu_OUT = SUB ? subtractor_1_out : 8'bz;  // Controlled_Buffer controlled_buffer_2
  assign Alu_OUT = A_B_AND ? and_1_out : 8'bz;  // Controlled_Buffer controlled_buffer_3
  assign Alu_OUT = A_B_OR ? or_1_out : 8'bz;  // Controlled_Buffer controlled_buffer_4
  assign Alu_OUT = A_B_XOR ? xor_1_out : 8'bz;  // Controlled_Buffer controlled_buffer_5
  assign Alu_OUT = A_NOT ? not_1_out : 8'bz;  // Controlled_Buffer controlled_buffer_6
endmodule

module instruction_decoder (
  input  [7:0] Data_In,
  output [3:0] Opcode,
  output [3:0] Operand
);


  assign Opcode = Data_In[7:4];
  assign Operand = Data_In[3:0];
endmodule

module jump_control (
  input  [7:0] Data_In,
  input  Zero_flag,
  output PC_count,
  output PC_load,
  output A_load,
  output [7:0] bus_out
);

  wire and_1_out, comparator_1_eq, comparator_2_eq, or_1_out;
  wire [3:0] instruction_decoder_1_opcode, instruction_decoder_1_operand;

  instruction_decoder instruction_decoder_1 (
    .Data_In(Data_In), .Opcode(instruction_decoder_1_opcode), .Operand(instruction_decoder_1_operand));
  Comparator #(.width(4)) comparator_1 (
    .a(4'b1011), .b(instruction_decoder_1_opcode), .eq(comparator_1_eq));  // open: gt, lt
  Comparator #(.width(4)) comparator_2 (
    .a(4'b1010), .b(instruction_decoder_1_opcode), .eq(comparator_2_eq));  // open: gt, lt
  Comparator #(.width(4)) comparator_3 (.a(4'b0010), .b(instruction_decoder_1_opcode), .eq(A_load));  // open: gt, lt
  assign bus_out[3:0] = or_1_out ? instruction_decoder_1_operand : 4'bz;  // Controlled_Buffer controlled_buffer_1
  or or_1 (or_1_out, A_load, and_1_out, comparator_2_eq);
  and and_1 (and_1_out, comparator_1_eq, Zero_flag);
  or or_2 (PC_count, and_1_out, comparator_2_eq);
  assign bus_out[7:4] = or_1_out ? 4'b0000 : 4'bz;  // Controlled_Buffer controlled_buffer_2

  assign PC_load = PC_count;
endmodule

module Out_control (
  input  [7:0] Data_In,
  output a_out,
  output out_enable
);

  wire [3:0] instruction_decoder_1_opcode;

  instruction_decoder instruction_decoder_1 (
    .Data_In(Data_In), .Opcode(instruction_decoder_1_opcode));  // open: Operand
  Comparator #(.width(4)) comparator_1 (.a(4'b0001), .b(instruction_decoder_1_opcode), .eq(a_out));  // open: gt, lt

  assign out_enable = a_out;
endmodule

module Alu_control (
  input  [7:0] Data_In,
  output Alu_Not,
  output Alu_Xor,
  output Alu_Or,
  output Alu_And,
  output Alu_Sub,
  output Alu_Add,
  output Alu_out
);

  wire [3:0] instruction_decoder_1_opcode;

  instruction_decoder instruction_decoder_1 (
    .Data_In(Data_In), .Opcode(instruction_decoder_1_opcode));  // open: Operand
  Comparator #(.width(4)) comparator_1 (.a(4'b1001), .b(instruction_decoder_1_opcode), .eq(Alu_Not));  // open: gt, lt
  Comparator #(.width(4)) comparator_2 (.a(4'b1000), .b(instruction_decoder_1_opcode), .eq(Alu_Xor));  // open: gt, lt
  Comparator #(.width(4)) comparator_3 (.a(4'b0111), .b(instruction_decoder_1_opcode), .eq(Alu_Or));  // open: gt, lt
  Comparator #(.width(4)) comparator_4 (.a(4'b0110), .b(instruction_decoder_1_opcode), .eq(Alu_And));  // open: gt, lt
  Comparator #(.width(4)) comparator_5 (.a(4'b0101), .b(instruction_decoder_1_opcode), .eq(Alu_Sub));  // open: gt, lt
  Comparator #(.width(4)) comparator_6 (.a(4'b0100), .b(instruction_decoder_1_opcode), .eq(Alu_Add));  // open: gt, lt
  or or_1 (Alu_out, Alu_Not, Alu_Xor, Alu_Or, Alu_And, Alu_Sub, Alu_Add);
endmodule

module SWP (
  input  [7:0] Data_In,
  input  [7:0] A,
  input  [7:0] B,
  input  CLOCK,
  input  Reset,
  output A_store,
  output B_store,
  output [7:0] A_out,
  output [7:0] B_out
);

  wire [3:0] instruction_decoder_1_opcode;

  instruction_decoder instruction_decoder_1 (
    .Data_In(Data_In), .Opcode(instruction_decoder_1_opcode));  // open: Operand
  Comparator #(.width(4)) comparator_1 (.a(4'b0011), .b(instruction_decoder_1_opcode), .eq(A_store));  // open: gt, lt
  Register register_1 (.D(A), .en(A_store), .clk(CLOCK), .Q(B_out), .clr(Reset));
  Register register_2 (.D(B), .en(A_store), .clk(CLOCK), .Q(A_out), .clr(Reset));

  assign B_store = A_store;
endmodule

module In_control (
  input  [7:0] Data_in,
  output Input_out,
  output Input_ENB,
  output A_Load
);

  wire [3:0] instruction_decoder_1_opcode;

  instruction_decoder instruction_decoder_1 (
    .Data_In(Data_in), .Opcode(instruction_decoder_1_opcode));  // open: Operand
  Comparator #(.width(4)) comparator_1 (.a(4'b0000), .b(instruction_decoder_1_opcode), .eq(A_Load));  // open: gt, lt

  assign Input_ENB = A_Load;
  assign Input_out = A_Load;
endmodule

module CPU (
  input  Clock,
  input  [7:0] Rom_In,
  input  [7:0] Ram_Data_Out,
  input  Input_Done,
  input  Reset,
  input  [7:0] Input_In,
  output [3:0] Ram_Addr,
  output Ram_Write,
  output [7:0] Rom_Addr,
  output Ram_Out,
  output [7:0] Ram_Data_In,
  output [7:0] Display
);

  wire A_LOAD, A_OUT, A_Override, ALU_ADD, ALU_AND, alu_control_1_alu_out, ALU_NOT, ALU_OR, ALU_OUT, ALU_SUB,
       ALU_XOR, and_1_out, and_3_out, and_4_out, and_5_out, and_6_out, and_7_out, and_8_out, and_14_out,
       and_18_out, and_19_out, B_LOAD, comparator_1_eq, controlled_buffer_9_out, DISPLAY_ENB,
       in_control_1_a_load, in_control_1_input_enb, in_control_1_input_out, Input_on, Input_out, INST_LOAD,
       j_k_ff_1_qn, jump_bus_out, jump_control_1_a_load, jump_control_1_pc_count, jump_control_1_pc_load,
       not_1_out, not_2_out, not_3_out, not_4_out, not_5_out, not_6_out, not_7_out, not_8_out, not_9_out,
       not_10_out, not_11_out, not_12_out, not_13_out, not_14_out, not_15_out, not_16_out, or_2_out,
       or_4_out, out_control_1_a_out, out_control_1_out_enable, PC_COUNT, PC_LOAD, ram_control_1_a_store,
       register_1_q, ZERO_FLAG;
  wire [7:0] A, A_Data_In, alu_1_alu_out, B, B_Data_In, controlled_buffer_2_out, controlled_buffer_5_out,
       controlled_buffer_6_out, controlled_buffer_8_out, INST_OUTPUT, jump_bus, Ram_Out_t;

  assign Ram_Out_t = Ram_Out ? Ram_Data_Out : 8'bz;  // Controlled_Buffer controlled_buffer_1
  Register Instruction_Reg (.D(controlled_buffer_2_out), .en(INST_LOAD), .clk(Clock), .Q(INST_OUTPUT), .clr(Reset));
  J_K_Flip_Flop j_k_ff_1 (.J(1'b1), .K(1'b1), .clk(Clock), .Qn(j_k_ff_1_qn), .reset(Reset));  // open: Q, preset
  not not_1 (not_1_out, A[0]);
  and and_1 (and_1_out, not_1_out, not_2_out);
  not not_2 (not_2_out, A[1]);
  not not_3 (not_3_out, A[2]);
  not not_4 (not_4_out, A[3]);
  not not_5 (not_5_out, A[4]);
  not not_6 (not_6_out, A[5]);
  not not_7 (not_7_out, A[6]);
  not not_8 (not_8_out, A[7]);
  Alu alu_1 (
    .A_In(A), .B_In(B), .ADD(ALU_ADD), .SUB(ALU_SUB), .A_B_AND(ALU_AND), .A_B_OR(ALU_OR), .A_B_XOR(ALU_XOR),
    .A_NOT(ALU_NOT), .Alu_OUT(alu_1_alu_out));
  and and_2 (INST_LOAD, j_k_ff_1_qn, not_9_out);
  not not_9 (not_9_out, Input_on);
  and and_3 (and_3_out, and_1_out, not_3_out);
  assign controlled_buffer_2_out = INST_LOAD ? Rom_In : 8'bz;  // Controlled_Buffer controlled_buffer_2
  assign controlled_buffer_2_out = ALU_OUT ? alu_1_alu_out : 8'bz;  // Controlled_Buffer controlled_buffer_3
  and and_4 (and_4_out, and_3_out, not_4_out);
  and and_5 (and_5_out, and_4_out, not_5_out);
  not not_10 (not_10_out, A_Override);
  not not_11 (not_11_out, Ram_Out);
  assign controlled_buffer_2_out = jump_bus_out ? jump_bus : 8'bz;  // Controlled_Buffer controlled_buffer_4
  and and_6 (and_6_out, and_5_out, not_6_out);
  and and_7 (and_7_out, not_10_out, not_11_out);
  assign controlled_buffer_5_out = and_7_out ? controlled_buffer_2_out : 8'bz;  // Controlled_Buffer controlled_buffer_5
  assign controlled_buffer_6_out = DISPLAY_ENB ? controlled_buffer_2_out : 8'bz;  // Controlled_Buffer controlled_buffer_6
  and and_8 (and_8_out, and_6_out, not_7_out);
  and and_9 (ZERO_FLAG, and_8_out, not_8_out);
  assign controlled_buffer_5_out = A_Override ? A_Data_In : 8'bz;  // Controlled_Buffer controlled_buffer_7
  not not_12 (not_12_out, B_LOAD);
  assign controlled_buffer_8_out = not_12_out ? controlled_buffer_2_out : 8'bz;  // Controlled_Buffer controlled_buffer_8
  Counter PC (
    .clr(Reset), .load(PC_LOAD), .clk(controlled_buffer_9_out), .D(jump_bus), .Q(Rom_Addr));  // open: up, count, carry
  assign controlled_buffer_9_out = PC_COUNT ? Clock : 1'bz;  // Controlled_Buffer controlled_buffer_9
  not not_13 (not_13_out, INST_LOAD);
  and and_10 (A_OUT, not_13_out, out_control_1_a_out);
  Register u_A (.D(controlled_buffer_5_out), .en(A_LOAD), .clk(Clock), .Q(A), .clr(Reset));
  assign controlled_buffer_5_out = Ram_Out ? Ram_Out_t : 8'bz;  // Controlled_Buffer controlled_buffer_10
  Register u_B (.D(controlled_buffer_8_out), .en(B_LOAD), .clk(Clock), .Q(B), .clr(Reset));
  assign controlled_buffer_8_out = B_LOAD ? B_Data_In : 8'bz;  // Controlled_Buffer controlled_buffer_11
  Register Display_Reg (.D(controlled_buffer_6_out), .en(DISPLAY_ENB), .clk(Clock), .Q(Display), .clr(Reset));
  assign controlled_buffer_2_out = Input_out ? Input_In : 8'bz;  // Controlled_Buffer controlled_buffer_12
  and and_11 (DISPLAY_ENB, out_control_1_out_enable, not_13_out);
  assign controlled_buffer_2_out = A_OUT ? A : 8'bz;  // Controlled_Buffer controlled_buffer_13
  and and_12 (ALU_OUT, not_13_out, alu_control_1_alu_out);
  and and_13 (PC_LOAD, not_14_out, jump_control_1_pc_load);
  and and_14 (and_14_out, not_14_out, jump_control_1_a_load);
  jump_control jump_control_1 (
    .Zero_flag(ZERO_FLAG), .Data_In(INST_OUTPUT), .PC_count(jump_control_1_pc_count),
    .PC_load(jump_control_1_pc_load), .A_load(jump_control_1_a_load), .bus_out(jump_bus));
  Out_control out_control_1 (.Data_In(INST_OUTPUT), .a_out(out_control_1_a_out), .out_enable(out_control_1_out_enable));
  Alu_control alu_control_1 (
    .Data_In(INST_OUTPUT), .Alu_Not(ALU_NOT), .Alu_Xor(ALU_XOR), .Alu_Or(ALU_OR), .Alu_And(ALU_AND),
    .Alu_Sub(ALU_SUB), .Alu_Add(ALU_ADD), .Alu_out(alu_control_1_alu_out));
  SWP swp_1 (
    .Data_In(INST_OUTPUT), .A(A), .B(B), .CLOCK(Clock), .Reset(Reset), .A_store(A_Override),
    .B_store(B_LOAD), .A_out(A_Data_In), .B_out(B_Data_In));
  In_control in_control_1 (
    .Data_in(INST_OUTPUT), .Input_out(in_control_1_input_out), .Input_ENB(in_control_1_input_enb),
    .A_Load(in_control_1_a_load));
  Ram_control ram_control_1 (
    .Data_In(INST_OUTPUT), .A(A), .A_Store(ram_control_1_a_store), .Ram_Write(Ram_Write), .Ram_Read(Ram_Out),
    .Ram_Data(Ram_Data_In), .Ram_Addr(Ram_Addr));
  or or_1 (A_LOAD, ALU_OUT, and_14_out, register_1_q, A_Override, and_18_out);
  or or_2 (or_2_out, jump_control_1_pc_load, jump_control_1_a_load);
  Comparator comparator_1 (.a({8{1'b0}}), .b(Rom_In), .eq(comparator_1_eq));  // open: gt, lt
  and and_15 (jump_bus_out, not_13_out, or_2_out);
  and and_16 (Input_out, comparator_1_eq, in_control_1_input_out);
  and and_17 (Input_on, in_control_1_input_enb, comparator_1_eq);
  and and_18 (and_18_out, in_control_1_a_load, comparator_1_eq);
  not not_14 (not_14_out, INST_LOAD);
  or or_3 (PC_COUNT, and_19_out, Input_Done);
  and and_19 (and_19_out, or_4_out, not_15_out);
  not not_15 (not_15_out, Input_on);
  or or_4 (or_4_out, INST_LOAD, jump_control_1_pc_count);
  Register #(.width(1)) register_1 (
    .D(ram_control_1_a_store), .en(1'b1), .clk(Clock), .Q(register_1_q), .clr(not_16_out));
  not not_16 (not_16_out, ram_control_1_a_store);

  // Other names for the same wires on the sheet: B_Override = B_LOAD; Main_Clock = Clock; Ram_In[7:0] = Ram_Data_In;
  //   Ram_Enable = Ram_Out; Ram_Out_Enable = Ram_Out; Ram_Write_Enable = Ram_Write; ROM_DATA[7:0] = Rom_In;
  //   ROM_OUT = INST_LOAD
endmodule

module Ram_control (
  input  [7:0] Data_In,
  input  [7:0] A,
  output A_Store,
  output Ram_Write,
  output Ram_Read,
  output [7:0] Ram_Data,
  output [3:0] Ram_Addr
);

  wire or_1_out;
  wire [3:0] instruction_decoder_1_opcode, instruction_decoder_1_operand;

  instruction_decoder instruction_decoder_1 (
    .Data_In(Data_In), .Opcode(instruction_decoder_1_opcode), .Operand(instruction_decoder_1_operand));
  Comparator #(.width(4)) comparator_1 (.a(instruction_decoder_1_opcode), .b(4'b1110), .eq(A_Store));  // open: gt, lt
  Comparator #(.width(4)) comparator_2 (.a(instruction_decoder_1_opcode), .b(4'b1101), .eq(Ram_Write));  // open: gt, lt
  or or_1 (or_1_out, A_Store, Ram_Write);
  assign Ram_Addr = or_1_out ? instruction_decoder_1_operand : 4'bz;  // Controlled_Buffer controlled_buffer_1

  assign Ram_Data = A;
  assign Ram_Read = A_Store;
endmodule
